# Fritzing sketch PicoK7 (saved by Fritzing 0.9.6b)
breadboards: 2

parts:
  Part1 = Adafruit MicroSD card breakout board [part_number="Adafruit #254"]
  RE1 = KY-040 Rotary encoder [package="Breakout board"]
  LCD_12864-06D1 = 128 x 64 Graphic LCD [part_number="CMG 12864-06D"]
  Q1 = NPN-Transistor [package="TO92 [THT]"]
  R1 = Resistor [tolerance=±5% power=0.25 resistance=220 package=THT]
  R2 = Resistor [tolerance=±5% power=0.25 resistance=1k package=THT]
  R3 = Resistor [tolerance=±5% power=0.25 resistance=100 package=THT]  # not connected
  U1 = AUDIO-JACK2 [package=audio-jack]
  A1 = Waveshare rp2040-zero tht [package=THT]

nets:
  N1: Part1.VCC, A1.Pin_1
  GND: Part1.GND, RE1.GND, LCD_12864-06D1.7_GND, LCD_12864-06D1.9_LEDK, Q1.E, U1.SLEEVE, A1.Pin_2
  N2: Part1.CLK, A1.Pin_21
  N3: Part1.DO, A1.Pin_23
  N4: Part1.DI, A1.Pin_20
  N5: Part1.CS, A1.Pin_22
  N6: RE1.Vcc, LCD_12864-06D1.6_VDD, R1.Pin_0, A1.Pin_3
  N7: RE1.SW, A1.Pin_19
  N8: RE1.DT, A1.Pin_18
  N9: RE1.CLK, A1.Pin_17
  N10: LCD_12864-06D1.1_/CS, A1.Pin_5
  N11: LCD_12864-06D1.2_RES, A1.Pin_6
  N12: LCD_12864-06D1.3_RS, A1.Pin_7
  N13: LCD_12864-06D1.4_SCK, A1.Pin_9
  N14: LCD_12864-06D1.5_SI, A1.Pin_8
  N15: LCD_12864-06D1.8_LEDA, R1.Pin_1
  N16: Q1.B, R2.Pin_0
  N17: Q1.C, U1.TIP
  N18: R2.Pin_1, A1.Pin_4

custom parts:
  Adafruit MicroSD card breakout board: Not just a simple breakout board, this microSD adapter goes the extra mile - designed for ease of use. Onboard 5v->3v regulator provides 150mA for power-hungry cards 3v level shifting means you can use this with ease on either 3v or 5v systems Uses a proper level shifting chip, not resistors: less problems, and faster read/write access Use 3 or 4 digital pins to read and write 2Gb+ of storage!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
  KY-040 Rotary encoder: KY-040 Rotary Encoder with switch on breakout borad from AZ Delivery
  128 x 64 Graphic LCD: Graphic LCD display 128x64 resolution ST7565R controller, 16S1Y / ER3805-1 SPI font ROM
  Waveshare rp2040-zero tht: .RP2040-Zero, A Low-Cost, High-Performance Pico-Like MCU Board Based On Raspberry Pi Microcontroller RP2040. This varant is THT without the extra connections.
